# Fritzing sketch EEPROM_ESP8266_ServoMotor (saved by Fritzing 0.9.3b)
breadboards: 1

parts:
  DHT1 = DHT11 Humitidy and Temperature Sensor (3 pins)
  M1 = CK-07 [package=THT]
  LED1 = RGB LED (com. cathode, rgb) [package="5 mm [THT]"]
  HC-SR04_Sensor_1 = HC-SR04 Ultrasonic Distance Sensor
  Amica_NodeMCU_DevKit_1_1 = Amica NodeMCU DevKit 1.0

nets:
  N1: DHT1.Plus, Amica_NodeMCU_DevKit_1_1.pin8
  N2: DHT1.Signal, HC-SR04_Sensor_1.VCC, Amica_NodeMCU_DevKit_1_1.pin_30
  GND: DHT1.Gnd, LED1.red_anode, HC-SR04_Sensor_1.GND, Amica_NodeMCU_DevKit_1_1.pin2, Amica_NodeMCU_DevKit_1_1.pin_9, Amica_NodeMCU_DevKit_1_1.pin_25, Amica_NodeMCU_DevKit_1_1.pin_29
  N3: M1.pin_1, Amica_NodeMCU_DevKit_1_1.pin_16
  N4: LED1.common_cathode, Amica_NodeMCU_DevKit_1_1.pin7
  N5: LED1.green_anode, Amica_NodeMCU_DevKit_1_1.pin6
  N6: LED1.blue_anode, Amica_NodeMCU_DevKit_1_1.pin5
  N7: HC-SR04_Sensor_1.TRIG, Amica_NodeMCU_DevKit_1_1.pin_14
  N8: HC-SR04_Sensor_1.ECHO, Amica_NodeMCU_DevKit_1_1.pin_13

custom parts:
  DHT11 Humitidy and Temperature Sensor (3 pins): DHT11 Humidity and Temperature Sensor (3 pins).
  CK-07: Fc-51 Infrared Obstacle Avoidance Proximity Sensor module. IR transmitter led, receiver LED, lm393 compaitor and a pot. 3.3 V to 5V power.
  RGB LED (com. cathode, rgb): A 5mm tri-color LED with red, green and blue inside.
  Amica NodeMCU DevKit 1.0: Amica NodeMCU DEVKIT 1.0 Development Kit based on ESP8266 ESP-12E, integating GPIO, PWM, IIC, 1-Wire and ADC all in one board.
